# Fritzing sketch Circuito Arduino uno (saved by Fritzing 0.9.3b)
breadboards: 1

parts:
  Componente1 = Arduino Uno (Rev3) - ICSP
  HC-SR04_Sensor_1 = HC-SR04 Ultrasonic Distance Sensor
  LoRa_Module1 = Ra-01 - LoRa Module SX1278 [part_number=SX1278]
  Componente2 = u-blox NEO-6M GPS Breakout

nets:
  N1: Componente1.ICSP_MISO, Componente1.D12/MISO, LoRa_Module1.MISO, Componente2.TXD
  N2: Componente1.ICSP_SCK, LoRa_Module1.SCK
  N3: Componente1.ICSP_MOSI, Componente1.D11_PWM/MOSI, LoRa_Module1.MOSI, Componente2.RXD
  N4: Componente1.D10_PWM/SS, LoRa_Module1.NSS
  N5: Componente1.D2, LoRa_Module1.DIO0
  N6: Componente1.D3_PWM, LoRa_Module1.DIO1
  N7: Componente1.D5_PWM, LoRa_Module1.RESET
  N8: Componente1.D6_PWM, HC-SR04_Sensor_1.ECHO
  N9: Componente1.D7, HC-SR04_Sensor_1.TRIG
  3V3: Componente1.3V3, LoRa_Module1.3.3V, Componente2.VCC
  5V: Componente1.5V, HC-SR04_Sensor_1.VCC
  GND: Componente1.GND, HC-SR04_Sensor_1.GND
  GND_2: LoRa_Module1.GND, Componente2.GND

custom parts:
  Ra-01 - LoRa Module SX1278: The Ra-01 LoRa Module featuring the SX1278 engine by Semtech. Module by AI-Thinker. Module (Ra-01) specifications from: https://www.banggood.com/Ra-01-Smart-Electronics-SX1278-LoRa-Spread-Spectrum-Wireless-Module-Ultra-Far-10KM-433M-p-1130769.html Description: Power supply: DC1.8-3.7V(3.3V) Chip: SX1278 Frequency: 433Mhz Operating temperature: -40~+85°C On Sheild Description (may vary by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
