# Fritzing sketch Circuito Dragino (saved by Fritzing 0.9.3b)

parts:
  Mod1 = Arduino Mega 2560 (Rev3)
  Componente1 = Dragino LoRa Shield V1.4
  HC-SR04_Sensor_1 = HC-SR04 Ultrasonic Distance Sensor

nets:
  N1: Mod1.D10_PWM, Componente1.10
  N2: Mod1.D9_PWM, Componente1.9
  5V: Mod1.5V, HC-SR04_Sensor_1.VCC
  GND: Mod1.GND, HC-SR04_Sensor_1.GND
  N3: Mod1.D2_PWM, Componente1.2
  N4: Mod1.D6_PWM, Componente1.6
  N5: Mod1.D7_PWM, Componente1.7
  N6: Mod1.D30, HC-SR04_Sensor_1.ECHO
  N7: Mod1.D31, HC-SR04_Sensor_1.TRIG
